# Fritzing sketch neopixel-with-pir (saved by Fritzing 0.9.2b)
breadboards: 1

parts:
  Raspberry_Pi1 = Raspberry Pi B+
  R1 = Resistor [tolerance=±5% resistance=2.2k package=THT]
  X4 = USB Connectors [package=s4b-ph]
  R2 = Resistor [tolerance=±5% resistance=470 package=THT]
  Q1 = 2N7000 FET N-Channel [part_number=2N7000 package=TO92]
  JP1 = Header 3 [package=screwterminal-3.5mm-3_lock.007s]

nets:
  N1: Raspberry_Pi1.GPIO18, R2.Pin_0
  GND: Raspberry_Pi1.GND, X4.GND, Q1.source, JP1.3
  N2: R1.Pin_0, X4.VBUS, JP1.1
  N3: R1.Pin_1, Q1.drain, JP1.2
  N4: R2.Pin_1, Q1.gate

notes:
  FET is a N MOSFET
  2N7000

custom parts:
  2N7000 FET N-Channel: A 2N7000 MOSFET N-Channel Transistor
